# Fritzing sketch Untitled Sketch (saved by Fritzing 0.9.3b)
breadboards: 1

parts:
  Q1 = PNP-Transistor [package="TO92 [THT]"]  # not connected
  Bauteil1 = Arduino Nano (Rev3.0) (ICSP)
  LCD1 = LCD screen
  R1 = Resistor [tolerance=±5% resistance=220 package=THT]
  R2 = Resistor [tolerance=±5% resistance=220 package=THT]
  R3 = Resistor [tolerance=±5% resistance=220 package=THT]
  R4 = Resistor [tolerance=±5% resistance=220 package=THT]
  R5 = Resistor [tolerance=±5% resistance=220 package=THT]
  LED1 = LED - 5mm [color="Red (633nm)" package="5 mm [THT]"]
  LED2 = LED - 5mm [color="Yellow (585nm)" package="5 mm [THT]"]
  LED3 = LED - 5mm [color="Green (560nm)" package="5 mm [THT]"]
  LED4 = LED - 5mm [color="Blue (470nm)" package="5 mm [THT]"]
  S1 = Taiway 100-SP-X-T1 SPDT Miniature Toggle Switch [part_number=100-SP-X-T1-0-0-B1-M1 package=THT]

nets:
  N1: Bauteil1.D3, LCD1.R/W
  N2: Bauteil1.D7, LCD1.DB6
  N3: Bauteil1.D9, R5.Pin_1
  N4: Bauteil1.D10, R4.Pin_1
  N5: Bauteil1.D11/MOSI, R3.Pin_1
  N6: LCD1.VSS, LCD1.DB5, LCD1.DB7, LCD1.LED-, LED1.anode, LED2.anode, LED3.anode, LED4.anode, S1.COM
  N7: LCD1.VDD, LCD1.V0
  N8: LCD1.DB3, LCD1.DB4
  N9: LCD1.LED+, R1.Pin_0
  N10: R2.Pin_0, LED4.cathode
  N11: R3.Pin_0, LED1.cathode
  N12: R4.Pin_0, LED2.cathode
  N13: R5.Pin_0, LED3.cathode

custom parts:
  PNP-Transistor: A standard PNP signal transistor
